# Fritzing sketch WALLE (saved by Fritzing 0.9.3b)
breadboards: 1

parts:
  Part1 = Arduino Uno (Rev3)
  J1 = Basic Servo
  J2 = Basic Servo
  L298N1 = L298N DC motor driver
  Part2 = Bluetooth HC-05 Macho
  BAT1 = BC9VPC [package=bc9vpc]
  M1 = DC Motor
  M2 = DC Motor

nets:
  N1: Part1.D8, L298N1.IN1
  N2: Part1.D9_PWM, L298N1.ENA
  N3: Part1.D10_PWM/SS, J2.pulse
  N4: Part1.D11_PWM/MOSI, J1.pulse
  GND: Part1.GND, J1.gnd, J2.gnd, L298N1.GND, Part2.GND, BAT1.V-
  N5: Part1.D0/RX, Part2.TXD
  N6: Part1.D1/TX, Part2.RXD
  N7: Part1.D3_PWM, L298N1.ENB
  N8: Part1.D4, L298N1.IN4
  N9: Part1.D5_PWM, L298N1.IN3
  N10: Part1.D7, L298N1.IN2
  VCC: Part1.5V, J1.vcc, J2.vcc, Part2.VCC
  N11: L298N1.OUT1, M2.pin_2
  N12: L298N1.OUT2, M2.pin_1
  N13: L298N1.OUT3, M1.pin_2
  N14: L298N1.OUT4, M1.pin_1
  N15: L298N1.12V, BAT1.V+

custom parts:
  L298N DC motor driver: 2x DC motor driver with 78M05 positive voltage regulator (7..35 V) L298N: max 46 V, 2 A Set 5 V Enable jumper to enable 5 V regultor (needed for the L298N) and +5 V output at screw terminal or supply external +5 V at screw terminal Set ENA and/or ENB to +5 V to enable motor permanently or supply ENA and/or ENB with PWM signal IN1 and IN2 set rotation directory for motor A (OUT1/OUT2) IN2 and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
